# Fritzing sketch ledControlOverInternet (saved by Fritzing 0.9.3b)
breadboards: 1

parts:
  LED1 = LED - 3mm [color="Red (633nm)" package="3 mm [THT]"]
  LED2 = LED - 3mm [color="Green (570nm)" package="3 mm [THT]"]
  LED3 = LED - 3mm [color="Yellow (595nm)" package="3 mm [THT]"]
  U1 = NodeMCU V1.0

nets:
  N1: LED1.cathode, LED2.cathode, LED3.cathode, U1.GND
  N2: LED1.anode, U1.D1
  N3: LED2.anode, U1.D0
  N4: LED3.anode, U1.D2

notes:
  NodeMCU
  Breadboard

custom parts:
  NodeMCU V1.0: ESP8266 based NodeMCU
